# Fritzing sketch Panner.02 (saved by Fritzing 0.9.3b)
breadboards: 1

parts:
  Teensy_3_2 = Teensy 3.1
  TMC2100 = Pololu A4988 [package=SO16]
  M1 = Stepper Motor - Bipolar
  J1 = screw terminal, 4 pins
  1_3"_128X64_OLED = Grove OLED 128x96
  R1 = Resistor [tolerance=±5% resistance=4.7k package=THT]
  R2 = Resistor [tolerance=±5% resistance=4.7k package=THT]
  C1 = Electrolytic Capacitor [capacitance=0.1mF voltage=20V package="300 mil [THT, electrolytic]"]
  ThumbStick = Thumb Joystick
  R3 = Resistor [tolerance=±5% resistance=22k package=THT]
  R4 = Resistor [tolerance=±5% resistance=4.7k package=THT]

nets:
  GND: Teensy_3_2.GND, Teensy_3_2.AGND, TMC2100.GND, 1_3"_128X64_OLED.GND, C1.-, ThumbStick.GND, R4.Pin_1
  N1: Teensy_3_2.D3, TMC2100.STEP
  N2: Teensy_3_2.D6, TMC2100.DIR
  3.3V: Teensy_3_2.3V3, TMC2100.VDD, 1_3"_128X64_OLED.VCC, R1.Pin_0, R2.Pin_0, ThumbStick.VCC
  N3: Teensy_3_2.A0/D14, R3.Pin_1, R4.Pin_0
  N4: Teensy_3_2.A1/D15, ThumbStick.HORZ
  N5: Teensy_3_2.A2/D16, ThumbStick.VERT
  N6: Teensy_3_2.A3/D17, ThumbStick.SEL
  N7: Teensy_3_2.A4/D18, 1_3"_128X64_OLED.SDA, R1.Pin_1
  N8: Teensy_3_2.A5/D19, 1_3"_128X64_OLED.SCL, R2.Pin_1
  5V: Teensy_3_2.Vin
  N9: TMC2100.1B, M1.C, J1.pin4
  N10: TMC2100.1A, M1.A, J1.pin3
  N11: TMC2100.2A, M1.B, J1.pin2
  N12: TMC2100.2B, M1.D, J1.pin1
  18V: TMC2100.VMOT, C1.+, R3.Pin_0
