# Fritzing sketch Panner.03 (saved by Fritzing 0.9.3b)
breadboards: 1

parts:
  Teensy_3_2 = Teensy 3.1
  ThumbStick = Thumb Joystick
  R3 = Resistor [tolerance=±5% resistance=22k package=THT]
  R4 = Resistor [tolerance=±5% resistance=4.7k package=THT]
  M1 = Stepper Motor - Bipolar
  C1 = Electrolytic Capacitor [capacitance=100µF voltage=35V package="300 mil [THT, electrolytic]"]
  LM1 = RioRand LM2596
  TMC2100 = Pololu A4988 [package=SO16]
  J1 = screw terminal, 4 pins
  TFT3 = Color 320x240 TFT Display, ILI9341 Controller Chip
  R5 = Resistor [tolerance=±5% resistance=100 package=THT]

nets:
  GND: Teensy_3_2.GND, Teensy_3_2.AGND, ThumbStick.GND, R4.Pin_1, C1.-, LM1.Pin_1, LM1.Pin_3, TMC2100.GND, TFT3.GND
  N1: Teensy_3_2.D3, TMC2100.STEP
  N2: Teensy_3_2.D4, TMC2100.ENABLE
  N3: Teensy_3_2.D6, TMC2100.DIR
  N4: Teensy_3_2.D9, TFT3.D/C
  N5: Teensy_3_2.D10, TFT3.CS
  N6: Teensy_3_2.D11, TFT3.SDI_(MOSI)
  N7: Teensy_3_2.D12, TFT3.SDO_(MISO)
  3.3V: Teensy_3_2.3V3, ThumbStick.VCC, TMC2100.VDD, TFT3.Reset
  N8: Teensy_3_2.D13, TFT3.SCK
  N9: Teensy_3_2.A0/D14, R3.Pin_1, R4.Pin_0
  N10: Teensy_3_2.A7/D21, ThumbStick.SEL
  N11: Teensy_3_2.A8/D22, ThumbStick.VERT
  N12: Teensy_3_2.A9/D23, ThumbStick.HORZ
  5V: Teensy_3_2.Vin, LM1.Pin_2, TFT3.VCC, R5.Pin_0
  18V: R3.Pin_0, C1.+, LM1.Pin_0, TMC2100.VMOT
  N13: M1.A, TMC2100.1A, J1.pin3
  N14: M1.C, TMC2100.1B, J1.pin4
  N15: M1.B, TMC2100.2A, J1.pin2
  N16: M1.D, TMC2100.2B, J1.pin1
  N17: TFT3.LED, R5.Pin_1

notes:
  3.3V
  5V

custom parts:
  Color 320x240 TFT Display, ILI9341 Controller Chip: 2.2" TFT Display with ILI9341 Controller
