# Fritzing sketch Panner.04 (saved by Fritzing 0.9.3b)
circuit board: 9.02616cm x 6.74913cm
breadboards: 1

parts:
  TMC2100 = Pololu A4988 [package=SO16]
  TFT1 = Color 320x240 TFT Display, ILI9341 Controller Chip
  S_B = Momentary Switch [package=ksa_sealed_tac_switch]
  S_A = Momentary Switch [package=ksa_sealed_tac_switch]
  R5 = Resistor [tolerance=±5% resistance=430 package=THT]
  R4 = Resistor [tolerance=±5% resistance=2.2k package=THT]
  R6 = Resistor [tolerance=±5% resistance=560 package=THT]
  R9 = Resistor [tolerance=±5% resistance=4.7k package=THT]
  R10 = Resistor [tolerance=±5% resistance=22k package=THT]
  R8 = Resistor [tolerance=±5% resistance=2.2k package=THT]
  J1 = screw terminal, 4 pins
  M1 = Stepper Motor - Bipolar
  C1 = Electrolytic Capacitor [capacitance=100µF voltage=35V package="300 mil [THT, electrolytic]"]
  LM1 = RioRand LM2596
  R3 = Resistor [tolerance=±5% resistance=4.7k package=THT]
  C2 = Electrolytic Capacitor [capacitance=100µF voltage=10V package="100 mil [THT, electrolytic]"]
  R7 = Resistor [tolerance=±5% resistance=1.2k package=THT]
  S_Nav = JOYSTICK_MINI [package=joystick_mini]
  R1 = Resistor [tolerance=±5% resistance=100 package=THT]
  Teensy_3_2 = Teensy 3.1
  R2 = Resistor [tolerance=±5% resistance=22k package=THT]

nets:
  N1: TMC2100.ENABLE, Teensy_3_2.D4
  N2: TMC2100.STEP, Teensy_3_2.D3
  N3: TMC2100.DIR, Teensy_3_2.D6
  GND: TMC2100.GND, TFT1.GND, C1.-, LM1.Pin_1, LM1.Pin_3, C2.-, Teensy_3_2.GND
  3.3V: TMC2100.VDD, TFT1.VCC, TFT1.Reset, R4.Pin_0, Teensy_3_2.3V3
  N4: TMC2100.1B, J1.pin4, M1.C
  N5: TMC2100.1A, J1.pin3, M1.A
  N6: TMC2100.2A, J1.pin2, M1.B
  N7: TMC2100.2B, J1.pin1, M1.D
  18V: TMC2100.VMOT, C1.+, LM1.Pin_0, R2.Pin_0
  N8: TFT1.CS, Teensy_3_2.D10
  N9: TFT1.D/C, Teensy_3_2.D9
  N10: TFT1.SDI_(MOSI), Teensy_3_2.D11
  N11: TFT1.SCK, Teensy_3_2.D13
  N12: TFT1.LED, R1.Pin_1
  N13: TFT1.SDO_(MISO), Teensy_3_2.D12
  N14: S_B.1, S_B.2, S_A.3, S_A.4, R3.Pin_1, S_Nav.GND, Teensy_3_2.AGND
  N15: S_B.3, S_B.4, R10.Pin_1
  N16: S_A.1, S_A.2, R9.Pin_1, R10.Pin_0
  N17: R5.Pin_0, R4.Pin_1, S_Nav.RIGHT, Teensy_3_2.A1/D15
  N18: R5.Pin_1, R6.Pin_0, S_Nav.UP
  N19: R6.Pin_1, R7.Pin_0, S_Nav.DOWN
  N20: R9.Pin_0, R8.Pin_1, S_Nav.CENT
  N21: R8.Pin_0, R7.Pin_1, S_Nav.LEFT
  5V: LM1.Pin_2, C2.+, R1.Pin_0, Teensy_3_2.Vin
  N22: R3.Pin_0, Teensy_3_2.A0/D14, R2.Pin_1

notes:
  3.3V
  5V

custom parts:
  Color 320x240 TFT Display, ILI9341 Controller Chip: 2.2" TFT Display with ILI9341 Controller
