# Fritzing sketch Panner.06 (saved by Fritzing 0.9.3b)
circuit board: 8.02452cm x 6.67428cm
breadboards: 1

parts:
  TMC2100 = Pololu A4988 [package=SO16]
  C2 = Electrolytic Capacitor [capacitance=100µF voltage=10V package="100 mil [THT, electrolytic]"]
  R10 = Resistor [tolerance=±5% resistance=100 package=THT]
  Teensy_3_2 = Teensy 3.1
  TFT1 = Color 320x240 TFT Display, ILI9341 Controller Chip
  S_A = Momentary Switch [package=ksa_sealed_tac_switch]
  R6 = Resistor [tolerance=±5% resistance=2.4k package=THT]
  R5 = Resistor [tolerance=±5% resistance=1.3k package=THT]
  R3 = Resistor [tolerance=±5% resistance=510 package=THT]
  S_Nav = JOYSTICK_MINI [package=joystick_mini]
  R4 = Resistor [tolerance=±5% resistance=750 package=THT]
  R7 = Resistor [tolerance=±5% resistance=7.5k package=THT]
  S_B = Momentary Switch [package=ksa_sealed_tac_switch]
  R1 = Resistor [tolerance=±5% resistance=2.2k package=THT]
  R2 = Resistor [tolerance=±5% resistance=360 package=THT]
  C1 = Electrolytic Capacitor [capacitance=100µF voltage=35V package="300 mil [THT, electrolytic]"]
  J2 = screw terminal, 4 pins
  R8 = Resistor [tolerance=±5% resistance=67k package=THT]
  R9 = Resistor [tolerance=±5% resistance=6.8k package=THT]
  J1 = Power Jack [package=power_jack_pth_lock]
  M1 = Stepper Motor - Bipolar
  U3 = Header 12 [package=1x12_machine-pin-header_lock.004]  # not connected
  U2 = Header 12 [package=1x12_machine-pin-header_lock.004]  # not connected
  U4 = Header 12 [package=1x12_machine-pin-header_lock.004]  # not connected
  U1 = Header 12 [package=1x12_machine-pin-header_lock.004]  # not connected
  R12 = Resistor [tolerance=±5% resistance=10k package=THT]
  R14 = Resistor [tolerance=±5% resistance=10k package=THT]
  MP1584EN = MP1584EN Power Regulator Board [part_number=MP1584EN]

nets (from the schematic view):
  N1: TMC2100.ENABLE, Teensy_3_2.D4
  N2: TMC2100.STEP, Teensy_3_2.D3
  N3: TMC2100.DIR, Teensy_3_2.D6
  GND: TMC2100.GND, C2.-, Teensy_3_2.GND, TFT1.GND, C1.-, J1.GND, J1.GNDBREAK, MP1584EN.IN_-, MP1584EN.OUT_-#13
  3.3V: TMC2100.VDD, R10.Pin_0, Teensy_3_2.3V3, TFT1.VCC, TFT1.Reset, R1.Pin_0, R12.Pin_0, R14.Pin_0
  N4: TMC2100.1B, J2.pin4, M1.C
  N5: TMC2100.1A, J2.pin3, M1.A
  N6: TMC2100.2A, J2.pin2, M1.B
  N7: TMC2100.2B, J2.pin1, M1.D
  18V: TMC2100.VMOT, C1.+, R8.Pin_0, J1.PWR, MP1584EN.IN_+
  5V: C2.+, Teensy_3_2.Vin, MP1584EN.OUT_+
  N8: R10.Pin_1, TFT1.LED
  N9: Teensy_3_2.D9, TFT1.D/C
  N10: Teensy_3_2.D10, TFT1.CS, R12.Pin_1
  N11: Teensy_3_2.D11, TFT1.SDI_(MOSI), R14.Pin_1
  N12: Teensy_3_2.D12, TFT1.SDO_(MISO)
  N13: Teensy_3_2.D13, TFT1.SCK
  N14: Teensy_3_2.A0/D14, R8.Pin_1, R9.Pin_0
  N15: Teensy_3_2.A1/D15, S_Nav.RIGHT, R1.Pin_1, R2.Pin_0
  N16: Teensy_3_2.AGND, S_A.3, S_A.4, S_Nav.GND, S_B.1, S_B.2, R9.Pin_1
  N17: S_A.1, S_A.2, R6.Pin_1, R7.Pin_0
  N18: R6.Pin_0, R5.Pin_1, S_Nav.CENT
  N19: R5.Pin_0, S_Nav.LEFT, R4.Pin_1
  N20: R3.Pin_0, S_Nav.UP, R2.Pin_1
  N21: R3.Pin_1, S_Nav.DOWN, R4.Pin_0
  N22: R7.Pin_1, S_B.3, S_B.4

notes:
  3.3V
  5V

custom parts:
  Color 320x240 TFT Display, ILI9341 Controller Chip: 2.2" TFT Display with ILI9341 Controller
  MP1584EN Power Regulator Board: The MP1584EN is a high frequency step-down switching regulator. The input voltage range is 4.5V to 28V. The output voltage is set by the board's potentiometer.
