# Fritzing sketch Panner.08 (saved by Fritzing 0.9.3b)
circuit board: 8.42972cm x 6.94462cm
breadboards: 1

parts:
  Pan_TMC2100 = Pololu A4988 [package=SO16]
  C2 = Electrolytic Capacitor [capacitance=100µF voltage=10V package="100 mil [THT, electrolytic]"]
  R10 = Resistor [tolerance=±5% resistance=100 package=THT]
  Teensy_3_2 = Teensy 3.1
  TFT1 = Color 320x240 TFT Display, ILI9341 Controller Chip
  S_A = Momentary Switch [package=ksa_sealed_tac_switch]
  S_Nav = JOYSTICK_MINI [package=joystick_mini]
  R8 = Resistor [tolerance=±5% resistance=67k package=THT]
  R9 = Resistor [tolerance=±5% resistance=6.8k package=THT]
  J1 = Power Jack [package=power_jack_pth_lock]
  Pan_Motor = Stepper Motor - Bipolar
  MP1584EN = MP1584EN Power Regulator Board [part_number=MP1584EN]
  S_B = Momentary Switch [package=ksa_sealed_tac_switch]
  R12 = Resistor [tolerance=±5% resistance=10k package=THT]
  R14 = Resistor [tolerance=±5% resistance=10k package=THT]
  C1 = Electrolytic Capacitor [capacitance=200µF voltage=35V package="300 mil [THT, electrolytic]"]
  R1 = Resistor [tolerance=±5% resistance=2.2k package=THT]
  R2 = Resistor [tolerance=±5% resistance=360 package=THT]
  R3 = Resistor [tolerance=±5% resistance=510 package=THT]
  R4 = Resistor [tolerance=±5% resistance=750 package=THT]
  R5 = Resistor [tolerance=±5% resistance=1.3k package=THT]
  R6 = Resistor [tolerance=±5% resistance=2.4k package=THT]
  R7 = Resistor [tolerance=±5% resistance=7.5k package=THT]
  U1_1 = RJ45 Jack [package=rj45-8]
  U1_2 = RJ45 Jack [package=rj45-8]
  Tilt_TMC2101 = Pololu A4988 [package=SO16]
  Slide_TMC2102 = Pololu A4988 [package=SO16]
  Tilt_Motor = Stepper Motor - Bipolar
  Slide_Motor = Stepper Motor - Bipolar
  U2_2 = RJ45 Jack [package=rj45-8]
  U2_1 = RJ45 Jack [package=rj45-8]

nets:
  N1: Pan_TMC2100.ENABLE, Teensy_3_2.D0
  N2: Pan_TMC2100.STEP, Teensy_3_2.D3
  N3: Pan_TMC2100.DIR, Teensy_3_2.D6
  GND: Pan_TMC2100.GND, C2.-, Teensy_3_2.GND, TFT1.GND, J1.GND, J1.GNDBREAK, MP1584EN.IN_-, MP1584EN.OUT_-#13, C1.-, Tilt_TMC2101.GND, Slide_TMC2102.GND
  3.3V: Pan_TMC2100.VDD, R10.Pin_0, Teensy_3_2.3V3, TFT1.VCC, TFT1.Reset, R12.Pin_0, R14.Pin_0, R1.Pin_0, Tilt_TMC2101.VDD, Slide_TMC2102.VDD
  N4: Pan_TMC2100.1B, U1_1.5
  N5: Pan_TMC2100.1A, U1_1.4
  N6: Pan_TMC2100.2A, U1_1.6
  N7: Pan_TMC2100.2B, U1_1.3
  18V: Pan_TMC2100.VMOT, R8.Pin_0, J1.PWR, MP1584EN.IN_+, C1.+, Tilt_TMC2101.VMOT, Slide_TMC2102.VMOT
  5V: C2.+, Teensy_3_2.Vin, MP1584EN.OUT_+
  N8: R10.Pin_1, TFT1.LED
  N9: Teensy_3_2.D1, Tilt_TMC2101.ENABLE
  N10: Teensy_3_2.D2, Slide_TMC2102.ENABLE
  N11: Teensy_3_2.D4, Tilt_TMC2101.STEP
  N12: Teensy_3_2.D5, Slide_TMC2102.STEP
  N13: Teensy_3_2.D7, Tilt_TMC2101.DIR
  N14: Teensy_3_2.D8, Slide_TMC2102.DIR
  N15: Teensy_3_2.D9, TFT1.D/C
  N16: Teensy_3_2.D10, TFT1.CS, R12.Pin_1
  N17: Teensy_3_2.D11, TFT1.SDI_(MOSI), R14.Pin_1
  N18: Teensy_3_2.D12, TFT1.SDO_(MISO)
  N19: Teensy_3_2.D13, TFT1.SCK
  N20: Teensy_3_2.A0/D14, R8.Pin_1, R9.Pin_0
  N21: Teensy_3_2.A1/D15, S_Nav.RIGHT, R1.Pin_1, R2.Pin_0
  N22: Teensy_3_2.AGND, S_A.1, S_A.2, S_Nav.GND, R9.Pin_1, S_B.3, S_B.4
  N23: S_A.3, S_A.4, R6.Pin_1, R7.Pin_0
  N24: S_Nav.UP, R2.Pin_1, R3.Pin_0
  N25: S_Nav.LEFT, R4.Pin_1, R5.Pin_0
  N26: S_Nav.CENT, R5.Pin_1, R6.Pin_0
  N27: S_Nav.DOWN, R3.Pin_1, R4.Pin_0
  N28: Pan_Motor.A, U1_2.4
  N29: Pan_Motor.C, U1_2.5
  N30: Pan_Motor.B, U1_2.6
  N31: Pan_Motor.D, U1_2.3
  N32: S_B.1, S_B.2, R7.Pin_1
  N33: U1_1.1, Tilt_TMC2101.1B
  N34: U1_1.2, Tilt_TMC2101.1A
  N35: U1_1.7, Tilt_TMC2101.2B
  N36: U1_1.8, Tilt_TMC2101.2A
  N37: U1_2.1, Tilt_Motor.C
  N38: U1_2.2, Tilt_Motor.A
  N39: U1_2.7, Tilt_Motor.D
  N40: U1_2.8, Tilt_Motor.B
  N41: Slide_TMC2102.1B, U2_1.5
  N42: Slide_TMC2102.1A, U2_1.4
  N43: Slide_TMC2102.2A, U2_1.6
  N44: Slide_TMC2102.2B, U2_1.3
  N45: Slide_Motor.A, U2_2.4
  N46: Slide_Motor.C, U2_2.5
  N47: Slide_Motor.B, U2_2.6
  N48: Slide_Motor.D, U2_2.3

notes:
  3.3V
  5V

custom parts:
  Color 320x240 TFT Display, ILI9341 Controller Chip: 2.2" TFT Display with ILI9341 Controller
  MP1584EN Power Regulator Board: The MP1584EN is a high frequency step-down switching regulator. The input voltage range is 4.5V to 28V. The output voltage is set by the board's potentiometer.
